// Digital circuit TOP.dig as structural Verilog
module TOP (
  input  clk
);

  wire button_1_out, button_2_out, button_3_out, button_4_out, button_5_out, dipswitch_1_out;

  Button button_1 (.out(button_1_out));
  DipSwitch dipswitch_1 (.out(dipswitch_1_out));
  Button button_2 (.out(button_2_out));
  Button button_3 (.out(button_3_out));
  CORE core_1 (
    .GC(clk), .MC(button_1_out), .SWC(dipswitch_1_out), .GO(button_4_out), .RST(button_2_out),
    .CLR(button_5_out), .STALL(button_3_out));  // open: PC, MIPC
  Button button_4 (.out(button_4_out));
  Button button_5 (.out(button_5_out));

  // Notes on the sheet:
  //   clk: Hz: 50000
endmodule
